# Fritzing sketch clock-v2 (saved by Fritzing 0.9.3b)
breadboards: 1

parts:
  U1 = 556 [package=dil14]
  R1 = Resistor [tolerance=±5% resistance=1k package=THT]
  R2 = Resistor [tolerance=±5% resistance=1k package=THT]
  C1 = Ceramic Capacitor [capacitance=10nF package="100 mil [THT, multilayer]"]
  C2 = Electrolytic Capacitor [capacitance=1µF package="100 mil [THT, electrolytic]"]
  R3 = Resistor [tolerance=±5% resistance=1M package=THT]
  C3 = Ceramic Capacitor [capacitance=100nF package="100 mil [THT, multilayer]"]
  C4 = Ceramic Capacitor [capacitance=10nF package="100 mil [THT, multilayer]"]
  C5 = Ceramic Capacitor [capacitance=100nF package="100 mil [THT, multilayer]"]
  LED1 = LED - 5mm [color="Yellow (592nm)" package="5 mm [THT]"]
  R4 = Resistor [tolerance=±5% resistance=330 package=THT]
  S1 = Pushbutton [package="[THT]"]
  R5 = Resistor [tolerance=±5% resistance=10k package=THT]
  R6 = Resistor [tolerance=±5% resistance=330 package=THT]
  LED2 = LED - 5mm [color="Yellow (592nm)" package="5 mm [THT]"]
  R7 = Resistor [tolerance=±5% resistance=10k package=THT]
  R8 = Resistor [tolerance=±5% resistance=1k package=THT]
  U2 = prefix000074HC02_NOR_Gate [part_number=SN74HC02N]
  U3 = prefix000074HC00_NAND_Gate [part_number=SN74HC00N]
  R9 = Resistor [tolerance=±5% resistance=330 package=THT]
  LED3 = LED - 5mm [color="Red (633nm)" package="5 mm [THT]"]
  LED4 = LED - 5mm [color="Green (555nm)" package="5 mm [THT]"]
  LED5 = LED - 5mm [color="Blue (430nm)" package="5 mm [THT]"]
  R10 = Resistor [tolerance=±5% resistance=330 package=THT]
  R11 = Resistor [tolerance=±5% resistance=330 package=THT]
  LED6 = LED - 5mm [color="Blue (430nm)" package="5 mm [THT]"]
  R12 = Resistor [tolerance=±5% resistance=10k package=THT]
  R13 = Resistor [tolerance=±5% resistance=10k package=THT]
  R14 = Rotary Potentiometer (Small) [maximum_resistance=1MΩ package=THT]
  S2 = Pushbutton [package="[THT]"]
  C6 = Ceramic Capacitor [capacitance=10nF package="100 mil [THT, multilayer]"]

nets:
  N1: U1.DIS, U1.THR, R3.Pin_0, C3.0
  N2: U1.CV, C4.0
  N3: U1.RST, U1.RST2, U3.connector10
  N4: U1.OUT, LED2.anode, U3.connector3
  N5: U1.TRIG, R7.Pin_1, U2.connector1, U2.connector2, S2.Pin_3, S2.Pin_4
  N6: U1.GND, C1.0, C2.-, C3.1, C4.1, C5.1, R4.Pin_0, R5.Pin_1, R6.Pin_1, U2.connector6, U3.connector6, R9.Pin_0, R10.Pin_1, R11.Pin_0, R13.Pin_0, S2.Pin_1, S2.Pin_2
  N7: U1.TRIG2, U1.THR2, C2.+, R14.wiper
  N8: U1.OUT2, LED1.anode, U3.connector0
  N9: U1.CV2, C1.1
  N10: U1.DIS2, R2.Pin_1
  N11: U1.VCC, R1.Pin_1, R2.Pin_0, R3.Pin_1, C5.0, S1.Pin_1, S1.Pin_2, R7.Pin_0, U2.connector13, U3.connector13, R12.Pin_0, C6.0
  N12: R1.Pin_0, R14.leg1
  N13: LED1.cathode, R4.Pin_1
  N14: S1.Pin_3, S1.Pin_4, R5.Pin_0, U2.connector11
  N15: R6.Pin_0, LED2.cathode
  N16: R8.Pin_0, U2.connector7, C6.1
  N17: R8.Pin_1, U2.connector0
  N18: U2.connector3, LED6.anode
  N19: U2.connector4, U2.connector5, U3.connector7, LED5.anode
  N20: U2.connector8, U2.connector12, U3.connector4, LED3.anode
  N21: U2.connector9, U2.connector10, U3.connector1, LED4.anode
  N22: U3.connector2, U3.connector8
  N23: U3.connector5, U3.connector9
  N24: U3.connector11, R13.Pin_1
  N25: U3.connector12, R12.Pin_1
  N26: R9.Pin_1, LED3.cathode, LED4.cathode
  N27: LED5.cathode, R10.Pin_0
  N28: R11.Pin_1, LED6.cathode

notes:
  HLT
  CLK
  CLK'
  WAKE'
