# Fritzing sketch q-clock-v2 (saved by Fritzing 0.9.3b)
breadboards: 1

parts:
  R1 = Rotary Potentiometer (Small) [maximum_resistance=100kΩ package=THT]
  U1 = 556 [package=dil14]
  S1 = Pushbutton [package="[THT]"]
  IC1 = IC, DIP package, 14 pins [chip_label=74HC74]
  IC2 = IC, DIP package, 14 pins [chip_label=74HC86]
  IC3 = IC, DIP package, 14 pins [chip_label=74HC00]
  IC5 = IC, DIP package, 14 pins [chip_label=74HC02]
  S2 = Pushbutton [package="[THT]"]
  IC6 = IC, DIP package, 14 pins [chip_label=74HC74]
  R2 = Resistor [tolerance=±5% resistance=1k package=THT]
  R3 = Resistor [tolerance=±5% resistance=1k package=THT]
  C1 = Ceramic Capacitor [capacitance=100nF package="100 mil [THT, multilayer]"]
  C2 = Ceramic Capacitor [capacitance=100nF package="100 mil [THT, multilayer]"]
  R4 = Resistor [tolerance=±5% resistance=1k package=THT]
  C3 = Electrolytic Capacitor [capacitance=1µF package="100 mil [THT, electrolytic]"]
  C4 = Ceramic Capacitor [capacitance=10nF package="100 mil [THT, multilayer]"]
  R5 = Resistor [tolerance=±5% resistance=1M package=THT]
  R6 = Resistor [tolerance=±5% resistance=10k package=THT]
  R7 = Resistor [tolerance=±5% resistance=10k package=THT]

nets:
  N1: R1.leg1, U1.TRIG2, U1.THR2, C3.+
  N2: R1.wiper, R2.Pin_0
  N3: U1.DIS, R4.Pin_0, R5.Pin_0
  N4: U1.THR, U1.TRIG, C4.0, R5.Pin_1
  N5: U1.CV, C2.0
  N6: U1.RST, U1.RST2, U1.VCC, IC1.pin1, IC1.pin4, IC1.pin10, IC1.pin13, IC1.pin14, IC2.pin12, IC2.pin13, IC2.pin14, IC3.pin14, IC5.pin8, IC5.pin9, IC5.pin14, S2.Pin_1, S2.Pin_2, IC6.pin1, IC6.pin4, IC6.pin13, IC6.pin14, R3.Pin_0, R4.Pin_1, R7.Pin_1
  N7: U1.OUT, IC1.pin3, IC1.pin11
  N8: U1.GND, S1.Pin_1, S1.Pin_2, IC1.pin7, IC2.pin1, IC2.pin2, IC2.pin4, IC2.pin5, IC2.pin7, IC3.pin7, IC5.pin7, IC6.pin7, C1.0, C2.1, C3.-, C4.1, R6.Pin_0
  N9: U1.OUT2, IC3.pin10
  N10: U1.CV2, C1.1
  N11: U1.DIS2, R2.Pin_1, R3.Pin_1
  N12: S1.Pin_3, S1.Pin_4, IC6.pin10, R7.Pin_0
  N13: IC1.pin2, S2.Pin_3, S2.Pin_4, R6.Pin_1
  N14: IC1.pin5, IC1.pin12, IC2.pin10
  N15: IC1.pin8, IC6.pin12
  N16: IC1.pin9, IC2.pin9
  N17: IC2.pin8, IC3.pin13
  N18: IC3.pin1, IC3.pin11
  N19: IC3.pin2, IC3.pin8
  N20: IC3.pin3, IC3.pin4, IC3.pin5
  N21: IC3.pin6, IC5.pin3, IC5.pin5, IC6.pin3
  N22: IC3.pin9, IC6.pin9
  N23: IC3.pin12, IC6.pin8
  N24: IC5.pin1, IC5.pin11, IC5.pin12
  N25: IC5.pin2, IC6.pin2, IC6.pin6
  N26: IC5.pin6, IC6.pin5
  N27: IC5.pin13, IC6.pin11

notes:
  Primary
  "Inverted"
