# Fritzing sketch eeprom_burner (saved by Fritzing 0.9.3b)
breadboards: 1

parts:
  U2 = 74xx594
  U3 = 74xx594
  Part2 = Arduino Uno (Rev3)
  C1 = Ceramic Capacitor [capacitance=100nF package="200 mil [THT, multilayer]"]
  AT28C1 = 74HC [chip_label=IC]  # not connected
  AT28C2 = AT28C64 [chip_label=28C64]

nets:
  N1: U2.connector0, AT28C2.connector8
  N2: U2.connector1, AT28C2.connector7
  N3: U2.connector2, AT28C2.connector6
  N4: U2.connector3, AT28C2.connector5
  N5: U2.connector4, AT28C2.connector4
  N6: U2.connector5, AT28C2.connector3
  N7: U2.connector6, AT28C2.connector2
  N8: U2.connector7, U3.connector7, Part2.GND, C1.0, AT28C2.connector13, AT28C2.connector19
  N9: U2.connector8, U3.connector13
  N10: U2.connector9, U2.connector12, U2.connector15, U3.connector9, U3.connector12, U3.connector15, Part2.5V, C1.1, AT28C2.connector27
  N11: U2.connector10, U3.connector10, Part2.D13/SCK
  N12: U2.connector11, U3.connector11, Part2.D10_PWM/SS
  N13: U2.connector13, Part2.D11_PWM/MOSI
  N14: U2.connector14, AT28C2.connector9
  N15: U3.connector0, AT28C2.connector23
  N16: U3.connector1, AT28C2.connector20
  N17: U3.connector2, AT28C2.connector22
  N18: U3.connector3, AT28C2.connector1
  N19: U3.connector6, AT28C2.connector21
  N20: U3.connector14, AT28C2.connector24
  N21: Part2.D8, AT28C2.connector12
  N22: Part2.D9_PWM, AT28C2.connector14
  N23: Part2.A5/SCL, AT28C2.connector26
  N24: Part2.D2, AT28C2.connector18
  N25: Part2.D3_PWM, AT28C2.connector17
  N26: Part2.D4, AT28C2.connector16
  N27: Part2.D5_PWM, AT28C2.connector15
  N28: Part2.D6_PWM, AT28C2.connector10
  N29: Part2.D7, AT28C2.connector11
