# Fritzing sketch register (saved by Fritzing 0.9.3b)
breadboards: 1

parts:
  IC1 = 74HC245 [chip_label=74HC245]
  IC2 = 74HC173 [chip_label=74HC173]
  IC3 = 74HC173 [chip_label=74HC173]
  R1 = Resistor [tolerance=±5% resistance=10k package=THT]
  R2 = Resistor [tolerance=±5% resistance=10k package=THT]
  LED1 = LED - 3mm [color="Yellow (592nm)" package="3 mm [THT]"]
  LED2 = LED - 3mm [color="Yellow (592nm)" package="3 mm [THT]"]
  LED3 = LED - 3mm [color="Yellow (592nm)" package="3 mm [THT]"]
  LED4 = LED - 3mm [color="Yellow (592nm)" package="3 mm [THT]"]
  LED5 = LED - 3mm [color="Yellow (592nm)" package="3 mm [THT]"]
  LED6 = LED - 3mm [color="Yellow (592nm)" package="3 mm [THT]"]
  LED7 = LED - 3mm [color="Yellow (592nm)" package="3 mm [THT]"]
  LED8 = LED - 3mm [color="Yellow (592nm)" package="3 mm [THT]"]
  R3 = Resistor [tolerance=±5% resistance=330 package=THT]
  R4 = Resistor [tolerance=±5% resistance=330 package=THT]
  R5 = Resistor [tolerance=±5% resistance=330 package=THT]
  R6 = Resistor [tolerance=±5% resistance=330 package=THT]
  LED9 = LED - 5mm [color="Red (633nm)" package="5 mm [THT]"]
  R7 = Resistor [tolerance=±5% resistance=330 package=THT]
  R8 = Resistor [tolerance=±5% resistance=10k package=THT]
  C1 = Ceramic Capacitor [capacitance=100nF package="100 mil [THT, multilayer]"]

nets:
  N1: IC1.connector0, IC1.connector18, IC1.connector19, IC2.connector8, IC2.connector9, IC2.connector15, IC3.connector8, IC3.connector9, IC3.connector15, R2.Pin_0, R2.Pin_1, LED9.cathode, R7.Pin_1, R8.Pin_0, R8.Pin_1, C1.1
  N2: IC1.connector1, IC2.connector2, LED1.anode
  N3: IC1.connector2, IC2.connector3, LED2.anode
  N4: IC1.connector3, IC2.connector4, LED3.anode
  N5: IC1.connector4, IC2.connector5, LED4.anode
  N6: IC1.connector5, IC3.connector2, LED5.anode
  N7: IC1.connector6, IC3.connector3, LED6.anode
  N8: IC1.connector7, IC3.connector4, LED7.anode
  N9: IC1.connector8, IC3.connector5, LED8.anode
  N10: IC1.connector9, IC2.connector0, IC2.connector1, IC2.connector7, IC2.connector14, IC3.connector7, IC3.connector14, R1.Pin_0, R1.Pin_1, R3.Pin_0, R4.Pin_0, R5.Pin_0, R6.Pin_0, C1.0
  N11: IC1.connector10, IC3.connector10
  N12: IC1.connector11, IC3.connector11
  N13: IC1.connector12, IC3.connector12
  N14: IC1.connector13, IC3.connector13
  N15: IC1.connector14, IC2.connector10
  N16: IC1.connector15, IC2.connector11
  N17: IC1.connector16, IC2.connector12
  N18: IC1.connector17, IC2.connector13
  N19: IC2.connector6, IC3.connector6
  N20: LED1.cathode, LED2.cathode, R3.Pin_1
  N21: LED3.cathode, LED4.cathode, R4.Pin_1
  N22: LED5.cathode, LED6.cathode, R5.Pin_1
  N23: LED7.cathode, LED8.cathode, R6.Pin_1
  N24: LED9.anode, R7.Pin_0

notes:
  RESET
  LOAD'
  OUT'
  BUS
