# Fritzing sketch clock (saved by Fritzing 0.9.3b)
breadboards: 1

parts:
  U1 = 555 Timer [package="DIP8 [THT]"]
  R2 = Rotary Potentiometer (Small) [maximum_resistance=1MΩ package=THT]
  R3 = Resistor [tolerance=±5% resistance=1k package=THT]
  R1 = Resistor [tolerance=±5% resistance=1k package=THT]
  C2 = Electrolytic Capacitor [capacitance=1µF package="100 mil [THT, electrolytic]"]
  R4 = Resistor [tolerance=±5% resistance=1k package=THT]
  LED1 = LED - 3mm [color="Yellow (595nm)" package="3 mm [THT]"]
  C1 = Ceramic Capacitor [capacitance=10nF package="100 mil [THT, multilayer]"]
  C3 = Ceramic Capacitor [capacitance=100nF package="100 mil [THT, multilayer]"]
  S1 = Pushbutton [package="[THT]"]
  R5 = Resistor [tolerance=±5% resistance=10k package="0805 [SMD]"]
  U2 = 555 Timer [package="DIP8 [THT]"]
  R6 = Resistor [tolerance=±5% resistance=330k package="0603 [SMD]"]
  C5 = Ceramic Capacitor [capacitance=100nF package="100 mil [THT, multilayer]"]
  LED2 = LED - 3mm [color="Red (633nm)" package="3 mm [THT]"]
  R7 = Resistor [tolerance=±5% resistance=1k package="0603 [SMD]"]
  C6 = Ceramic Capacitor [capacitance=10nF package="100 mil [THT, multilayer]"]
  S2 = Toggle Switch [package=THT]
  R8 = Resistor [tolerance=±5% resistance=10k package=THT]
  R9 = Resistor [tolerance=±5% resistance=10k package=THT]
  U3 = prefix000074HC02_NOR_Gate [part_number=SN74HC02N]
  LED3 = LED - 3mm [color="Green (555nm)" package="3 mm [THT]"]
  LED4 = LED - 3mm [color="Red (633nm)" package="3 mm [THT]"]
  R10 = Resistor [tolerance=±5% resistance=1k package=THT]
  74xx1 = 74xx08 [part_number=74HC08]
  LED5 = LED - 3mm [color="Blue (525nm)" package="3 mm [THT]"]
  R11 = Resistor [tolerance=±5% resistance=1k package=THT]

nets:
  N1: U1.Ground, C2.-, R4.Pin_0, C1.0, C3.1, S1.Pin_3, S1.Pin_4, U2.Ground, C5.1, R7.Pin_1, C6.0, R8.Pin_1, R9.Pin_1, U3.connector6, R10.Pin_0, 74xx1.connector6, R11.Pin_1
  N2: U1.Trigger, U1.Threshold, R2.wiper, C2.+
  N3: U1.Output, LED1.anode, 74xx1.connector0
  N4: U1.Reset, U1.Vcc_Supply_Voltage, R1.Pin_0, C3.0, R5.Pin_0, U2.Reset, U2.Vcc_Supply_Voltage, R6.Pin_0, S2.COM, U3.connector1, U3.connector13, 74xx1.connector8, 74xx1.connector9, 74xx1.connector11, 74xx1.connector12, 74xx1.connector13
  N5: U1.Control_Voltage, C1.1
  N6: U1.Discharge, R3.Pin_1, R1.Pin_1
  N7: R2.leg1, R3.Pin_0
  N8: R4.Pin_1, LED1.cathode
  N9: S1.Pin_1, S1.Pin_2, R5.Pin_1, U2.Trigger
  N10: U2.Output, LED2.anode, 74xx1.connector3
  N11: U2.Control_Voltage, C6.1
  N12: U2.Threshold, U2.Discharge, R6.Pin_1, C5.0
  N13: LED2.cathode, R7.Pin_0
  N14: S2.L1, R9.Pin_0, U3.connector7
  N15: S2.L2, R8.Pin_0, U3.connector11
  N16: U3.connector0, LED5.anode
  N17: U3.connector2, U3.connector3
  N18: U3.connector4, 74xx1.connector2
  N19: U3.connector5, 74xx1.connector5
  N20: U3.connector8, U3.connector12, LED4.anode, 74xx1.connector4
  N21: U3.connector9, U3.connector10, LED3.anode, 74xx1.connector1
  N22: LED3.cathode, LED4.cathode, R10.Pin_1
  N23: LED5.cathode, R11.Pin_0

notes:
  Clock output: Blue LED
  Halt signal: Pink wire
