# Fritzing sketch eeprom_burner (saved by Fritzing 0.9.3b)
breadboards: 1

parts:
  U2 = 74xx594
  U3 = 74xx594
  AT28C1 = AT28C64 [chip_label=IC]
  Part1 = Arduino Nano (Rev3.0)

nets:
  N1: U2.connector0, AT28C1.connector8
  N2: U2.connector1, AT28C1.connector7
  N3: U2.connector2, AT28C1.connector6
  N4: U2.connector3, AT28C1.connector5
  N5: U2.connector4, AT28C1.connector4
  N6: U2.connector5, AT28C1.connector3
  N7: U2.connector6, AT28C1.connector2
  N8: U2.connector7, U3.connector7, AT28C1.connector13, AT28C1.connector19, Part1.GND
  N9: U2.connector8, U3.connector13
  N10: U2.connector9, U2.connector12, U2.connector15, U3.connector9, U3.connector12, U3.connector15, AT28C1.connector27, Part1.5V
  N11: U2.connector10, U2.connector11, U3.connector10, U3.connector11, Part1.D13/SCK
  N12: U2.connector13, Part1.D11/MOSI
  N13: U2.connector14, AT28C1.connector9
  N14: U3.connector0, AT28C1.connector23
  N15: U3.connector1, AT28C1.connector20
  N16: U3.connector2, AT28C1.connector22
  N17: U3.connector3, AT28C1.connector1
  N18: U3.connector5, AT28C1.connector21
  N19: U3.connector14, AT28C1.connector24
