// Logisim project mem-control.circ as structural Verilog: 1 circuit, main circuit main
module main (
  input  OUT,
  input  LOAD,
  output BOE,
  output DIR,
  output OE,
  output WE
);

  wire clock_1_out, nand_1_out;

  Clock clock_1 (.out(clock_1_out));
  nand nand_1 (nand_1_out, OUT, LOAD);
  nand nand_2 (DIR, LOAD, LOAD);
  nand nand_3 (BOE, nand_1_out, nand_1_out);
  nand nand_4 (WE, DIR, clock_1_out);

  assign OE = DIR;

  // Notes on the sheet:
  //   LOAD: pull=up
  //   OUT: pull=up
  //   Buffer Output Enable: LOW - transmit to or from main bus
  //   Buffer direction: LOW - to bus, HIGH - from bus
  //   RAM Output Enable, active LOW
  //   RAM Write Enable. active LOW
endmodule
