// Logisim project overflow.circ as structural Verilog: 1 circuit, main circuit main
module main (
  input  A,
  input  S,
  input  B,
  output out_4
);

  wire xor_1_out, xor_2_out;

  xor xor_1 (xor_1_out, A, S);
  xor xor_2 (xor_2_out, S, B);
  and and_1 (out_4, xor_1_out, xor_2_out);
endmodule
