// Digital circuit q-clock-v2.dig as structural Verilog
module q_clock_v2 (
  input  Scan,
  input  Clock,
  input  Brk,
  input  Halt,
  output Inverted,
  output Primary
);

  wire Auto_out, counter_1_ovf, counter_2_ovf, d_ff_1_nq, d_ff_1_q, d_ff_2_q, d_ff_3_nq, d_ff_3_q,
       d_ff_as_1_nq, d_ff_as_1_q, Manual_out, nand_1_out, nand_2_out, nand_3_out, nor_1_out, xor_1_out;
  wire [3:0] counter_1_out, counter_2_out, counter_3_out, counter_4_out;

  Button #(.activeLow("true")) Auto (.out(Auto_out));
  Button Manual (.out(Manual_out));
  D_FF d_ff_1 (.D(Manual_out), .C(Scan), .Q(d_ff_1_q), .nQ(d_ff_1_nq));
  D_FF d_ff_2 (.D(d_ff_1_q), .C(Scan), .Q(d_ff_2_q));  // open: nQ
  D_FF_AS d_ff_as_1 (.Set(~Auto_out), .D(d_ff_1_nq), .C(Primary), .Clr(~1'b1), .Q(d_ff_as_1_q), .nQ(d_ff_as_1_nq));
  xor xor_1 (xor_1_out, d_ff_1_q, d_ff_2_q);
  nand nand_1 (nand_1_out, Clock, d_ff_as_1_q);
  nand nand_2 (nand_2_out, d_ff_as_1_nq, xor_1_out);
  nand nand_3 (nand_3_out, nand_1_out, nand_2_out);
  nor nor_1 (nor_1_out, nand_3_out, Halt);
  D_FF d_ff_3 (.D(d_ff_3_nq), .C(nor_1_out), .Q(d_ff_3_q), .nQ(d_ff_3_nq));
  LED Mid_cycle (.in(d_ff_3_nq));
  nor nor_2 (Inverted, nor_1_out, d_ff_3_q);
  nor nor_3 (Primary, d_ff_3_nq, nor_1_out);
  Counter #(.Bits(4)) counter_1 (.en(1'b1), .C(Inverted), .clr(1'b0), .out(counter_1_out), .ovf(counter_1_ovf));
  Counter #(.Bits(4)) counter_2 (.en(1'b1), .C(Primary), .clr(1'b0), .out(counter_2_out), .ovf(counter_2_ovf));
  Counter #(.Bits(4)) counter_3 (.en(counter_1_ovf), .C(Inverted), .clr(1'b0), .out(counter_3_out));  // open: ovf
  Counter #(.Bits(4)) counter_4 (.en(counter_2_ovf), .C(Primary), .clr(1'b0), .out(counter_4_out));  // open: ovf
  Seven_Seg_Hex seven_seg_hex_1 (.d(counter_3_out), .dp(1'b0));
  Seven_Seg_Hex seven_seg_hex_2 (.d(counter_4_out), .dp(1'b0));
  Seven_Seg_Hex seven_seg_hex_3 (.d(counter_1_out), .dp(1'b0));
  Seven_Seg_Hex seven_seg_hex_4 (.d(counter_2_out), .dp(1'b0));

  // Notes on the sheet:
  //   Scan: Hz: 100
  //   Clock: Hz: 2
  //   Brk: default 1
endmodule
