// Logisim project q-clock.circ as structural Verilog: 1 circuit, main circuit main
module main (
  output A,
  output B
);

  wire clock_1_out, d_ff_1_q, d_ff_1_qn, nor_1_out;

  Clock clock_1 (.out(clock_1_out));
  nor nor_1 (nor_1_out, clock_1_out, clock_1_out);
  D_Flip_Flop d_ff_1 (.clk(nor_1_out), .D(d_ff_1_qn), .Q(d_ff_1_q), .Qn(d_ff_1_qn));  // open: preset, en, reset
  nor nor_2 (A, nor_1_out, d_ff_1_q);
  nor nor_3 (B, nor_1_out, d_ff_1_qn);
endmodule
