// Logisim project reg-alu.circ as structural Verilog: 1 circuit, main circuit main
module main (
);

  wire button_1_out, clock_1_out, not_1_out;
  wire [7:0] adder_1_out, register_1_q, register_2_q, register_3_q;

  Clock clock_1 (.out(clock_1_out));
  Button button_1 (.out(button_1_out));
  Register register_1 (.D(adder_1_out), .Q(register_1_q), .clk(clock_1_out));  // open: en, clr
  not not_1 (not_1_out, clock_1_out);
  Register register_2 (.D(8'h1), .en(button_1_out), .Q(register_2_q), .clk(clock_1_out));  // open: clr
  Register register_3 (.D(register_1_q), .Q(register_3_q), .clk(not_1_out));  // open: en, clr
  Adder adder_1 (.a(register_3_q), .b(register_2_q), .out(adder_1_out), .cin(1'b0));  // open: cout
  Hex_Digit_Display hex_digit_display_1 (.value(adder_1_out[7:4]));  // open: dp
  Hex_Digit_Display hex_digit_display_2 (.value(adder_1_out[3:0]));  // open: dp
endmodule
