// Digital circuit ud-counter.dig as structural Verilog
module ud_counter (
  input  nLoad,
  input  nDown,
  input  nUp,
  input  Primary,
  input  nOut
);

  wire _74193_1_pin11, _74193_1_pin12, _74193_1_pin13, nand_1_out, nand_2_out, nReset_out, or_1_out,
       or_2_out, or_3_out, or_4_out;
  wire [1:0] _74193_1_pin2, _74193_1_pin6;
  wire [3:0] _74193_2_pin2;

  nand nand_1 (nand_1_out, Primary, Primary);
  Button #(.activeLow("true")) nReset (.out(nReset_out));
  or or_1 (or_1_out, nOut, nand_1_out);
  or or_2 (or_2_out, nand_1_out, nLoad);
  Seven_Seg_Hex seven_seg_hex_1 (.d(_74193_2_pin2), .dp(1'b0));
  or or_3 (or_3_out, nDown, or_1_out);
  or or_4 (or_4_out, or_1_out, nUp);
  nand nand_2 (nand_2_out, or_2_out, nReset_out);
  _74193 _74193_1 (
    .pin1(1'b0), .pin2(_74193_1_pin2[1]), .pin3(_74193_1_pin2[0]), .pin4(or_3_out), .pin5(or_4_out),
    .pin6(_74193_1_pin6[0]), .pin7(_74193_1_pin6[1]), .pin8(1'b0), .pin9(1'b0), .pin10(1'b1),
    .pin11(_74193_1_pin11), .pin12(_74193_1_pin12), .pin13(_74193_1_pin13), .pin14(1'b0), .pin15(1'b1),
    .pin16(1'b1));
  nand nand_3 (_74193_1_pin11, nand_2_out, nand_2_out);
  Seven_Seg_Hex seven_seg_hex_2 (.d({_74193_1_pin6, _74193_1_pin2}), .dp(1'b0));
  _74193 _74193_2 (
    .pin1(1'b1), .pin2(_74193_2_pin2[1]), .pin3(_74193_2_pin2[0]), .pin4(_74193_1_pin13),
    .pin5(_74193_1_pin12), .pin6(_74193_2_pin2[2]), .pin7(_74193_2_pin2[3]), .pin8(1'b0), .pin9(1'b1),
    .pin10(1'b0), .pin11(_74193_1_pin11), .pin14(1'b0), .pin15(1'b0), .pin16(1'b1));  // open: pin12, pin13

  // Notes on the sheet:
  //   nLoad: default 1
  //   nDown: default 1
  //   nUp: default 1
  //   nOut: default 1
endmodule
