// Logisim project zero.circ as structural Verilog: 1 circuit, main circuit main
module main (
  input  D0,
  input  D1,
  input  D2,
  input  D3,
  input  D4,
  input  D5,
  input  D6,
  input  D7,
  output Z
);

  wire and_1_out, and_2_out, nor_1_out, nor_2_out, nor_3_out, nor_4_out;

  nor nor_1 (nor_1_out, D0, D1);
  nor nor_2 (nor_2_out, D2, D3);
  nor nor_3 (nor_3_out, D4, D5);
  nor nor_4 (nor_4_out, D6, D7);
  and and_1 (and_1_out, nor_1_out, nor_2_out);
  and and_2 (and_2_out, nor_3_out, nor_4_out);
  and and_3 (Z, and_1_out, and_2_out);
endmodule
